# Fritzing sketch Project_1_schematic (saved by Fritzing 0.7.12b)
breadboards: 1

parts:
  Raspberry_Pi1 = Raspberry Pi (Model B)
  LED1 = LED - 5mm [color="Red (633nm)" package="5 mm [THT]"]
  75R = Resistor [tolerance=±5% resistance=75 package=THT]

nets:
  N1: Raspberry_Pi1.3V3, 75R.Pin_0
  N2: LED1.anode, 75R.Pin_1

custom parts:
  Raspberry Pi (Model B): Raspberry Pi Single-board Computer, Model B
