# Fritzing sketch Project_10_schematic (saved by Fritzing 0.7.12b)
breadboards: 1

parts:
  Raspberry_Pi1 = Raspberry Pi (Model B)
  J1 = Piezo Speaker
  S1 = Pushbutton [package="[THT]"]
  R1 = Resistor [tolerance=±5% resistance=10k package=THT]

nets:
  N1: Raspberry_Pi1.GND, J1.pin1
  N2: Raspberry_Pi1.RXD, S1.Pin_3, S1.Pin_4, R1.Pin_1
  N3: Raspberry_Pi1.#18, J1.pin2
  N4: S1.Pin_1, S1.Pin_2

notes:
  10K

custom parts:
  Raspberry Pi (Model B): Raspberry Pi Single-board Computer, Model B
