# Fritzing sketch Project_3_schematic (saved by Fritzing 0.7.12b)
breadboards: 1

parts:
  Raspberry_Pi1 = Raspberry Pi (Model B)
  LED1 = LED - 5mm [color="Red (633nm)" package="5 mm [THT]"]
  R1 = Resistor [tolerance=±5% resistance=75 package=THT]

nets:
  N1: Raspberry_Pi1.RXD, R1.Pin_0
  N2: LED1.anode, R1.Pin_1

notes:
  75R

custom parts:
  Raspberry Pi (Model B): Raspberry Pi Single-board Computer, Model B
