# Fritzing sketch Project_4_schematic (saved by Fritzing 0.7.12b)
breadboards: 1

parts:
  Raspberry_Pi1 = Raspberry Pi (Model B)
  LED1 = LED - 5mm [color="Red (633nm)" package="5 mm [THT]"]
  R1 = Resistor [tolerance=±5% resistance=75 package=THT]
  S1 = Pushbutton [package="[THT]"]
  R2 = Resistor [tolerance=±5% resistance=10k package=THT]

nets:
  N1: Raspberry_Pi1.RXD, R1.Pin_0
  N2: Raspberry_Pi1.#18, S1.Pin_3, S1.Pin_4, R2.Pin_1
  N3: LED1.anode, R1.Pin_1
  N4: S1.Pin_1, S1.Pin_2

notes:
  75R
  10K

custom parts:
  Raspberry Pi (Model B): Raspberry Pi Single-board Computer, Model B
