# Fritzing sketch Project_5_schematic (saved by Fritzing 0.7.12b)
breadboards: 1

parts:
  Raspberry_Pi1 = Raspberry Pi (Model B)
  LED1 = LED - 5mm [color="Red (633nm)" package="5 mm [THT]"]
  R1 = Resistor [tolerance=±5% resistance=75 package=THT]
  S1 = Pushbutton [package="[THT]"]
  R2 = Resistor [tolerance=±5% resistance=10k package=THT]
  LED2 = LED - 5mm [color="Orange (612nm)" package="5 mm [THT]"]
  LED3 = LED - 5mm [color="Green (560nm)" package="5 mm [THT]"]
  R3 = Resistor [tolerance=±5% resistance=75 package=THT]
  R4 = Resistor [tolerance=±5% resistance=75 package=THT]

nets:
  N1: Raspberry_Pi1.GND, LED1.cathode
  N2: Raspberry_Pi1.RXD, R1.Pin_0
  N3: Raspberry_Pi1.#18, R4.Pin_0
  N4: Raspberry_Pi1.#23, R3.Pin_0
  N5: Raspberry_Pi1.#24, S1.Pin_3, S1.Pin_4, R2.Pin_1
  N6: LED1.anode, R1.Pin_1
  N7: S1.Pin_1, S1.Pin_2
  N8: LED2.anode, R4.Pin_1
  N9: LED3.anode, R3.Pin_1

notes:
  75R
  10K

custom parts:
  Raspberry Pi (Model B): Raspberry Pi Single-board Computer, Model B
