# Fritzing sketch Project_6_schematic (saved by Fritzing 0.7.12b)
breadboards: 1

parts:
  Raspberry_Pi1 = Raspberry Pi (Model B)
  DS1 = DS18B20 1-Wire Temperature Sensor [part_number=DS18B20]
  R1 = Resistor [tolerance=±5% resistance=10k package=THT]
  LED1 = LED - 5mm [color="Red (633nm)" package="5 mm [THT]"]
  LED2 = LED - 5mm [color="Green (565nm)" package="5 mm [THT]"]
  R2 = Resistor [tolerance=±5% resistance=75 package=THT]
  R3 = Resistor [tolerance=±5% resistance=75 package=THT]

nets:
  3V3: Raspberry_Pi1.3V3, DS1.VDD, R1.Pin_0
  GND: Raspberry_Pi1.GND, DS1.GND
  N1: Raspberry_Pi1.#4, DS1.DQ, R1.Pin_1
  N2: Raspberry_Pi1.#21, R2.Pin_0
  N3: Raspberry_Pi1.#22, R3.Pin_0
  N4: Raspberry_Pi1.#23, LED1.cathode
  N5: LED1.anode, R3.Pin_1
  N6: LED2.anode, R2.Pin_1

custom parts:
  Raspberry Pi (Model B): Raspberry Pi Single-board Computer, Model B
