# Fritzing sketch Project_7_schematic (saved by Fritzing 0.7.12b)
breadboards: 1

parts:
  Raspberry_Pi1 = Raspberry Pi (Model B)
  LED1 = LED - 5mm [color="Red (633nm)" package="5 mm [THT]"]
  LED2 = LED - 5mm [color="Green (565nm)" package="5 mm [THT]"]
  R2 = Resistor [tolerance=±5% resistance=75 package=THT]
  R3 = Resistor [tolerance=±5% resistance=75 package=THT]
  R4 = Photocell (LDR) [package=THT]
  LED3 = LED - 5mm [color="Orange (612nm)" package="5 mm [THT]"]
  R5 = Resistor [tolerance=±5% resistance=75 package=THT]
  C1 = Ceramic Capacitor [capacitance=220nF package="200 mil [THT, multilayer]"]

nets:
  N1: Raspberry_Pi1.3V3, R4.pin_0
  N2: Raspberry_Pi1.SDA, R2.Pin_0
  N3: Raspberry_Pi1.SCL, R5.Pin_0
  N4: Raspberry_Pi1.GND, C1.0
  N5: Raspberry_Pi1.#4, R3.Pin_0
  N6: Raspberry_Pi1.#18, R4.pin_1, C1.1
  N7: LED1.anode, R3.Pin_1
  N8: LED2.anode, R2.Pin_1
  N9: LED3.anode, R5.Pin_1

notes:
  220nf Capacitor
  LDR

custom parts:
  Raspberry Pi (Model B): Raspberry Pi Single-board Computer, Model B
