# Fritzing sketch Project_8_schematic (saved by Fritzing 0.7.12b)
breadboards: 1

parts:
  Raspberry_Pi1 = Raspberry Pi (Model B)
  LED1 = LED - 5mm [color="Red (633nm)" package="5 mm [THT]"]
  LED2 = LED - 5mm [color="Green (565nm)" package="5 mm [THT]"]
  R2 = Resistor [tolerance=±5% resistance=75 package=THT]
  R3 = Resistor [tolerance=±5% resistance=75 package=THT]

nets:
  N1: Raspberry_Pi1.GND, LED2.cathode
  N2: Raspberry_Pi1.#24, R2.Pin_0
  N3: Raspberry_Pi1.#25, R3.Pin_0
  N4: LED1.anode, R3.Pin_1
  N5: LED2.anode, R2.Pin_1

custom parts:
  Raspberry Pi (Model B): Raspberry Pi Single-board Computer, Model B
