# Fritzing sketch Project_9_schematic (saved by Fritzing 0.7.12b)
breadboards: 1

parts:
  Raspberry_Pi1 = Raspberry Pi (Model B)
  J1 = Piezo Speaker

nets:
  N1: Raspberry_Pi1.GND, J1.pin1
  N2: Raspberry_Pi1.#18, J1.pin2

notes:
  +V
  GND

custom parts:
  Raspberry Pi (Model B): Raspberry Pi Single-board Computer, Model B
